# Fritzing sketch initial_scetch (saved by Fritzing 0.9.3b)
circuit board: 8.46667cm x 5.64444cm
breadboards: 1

parts:
  Raspberry_Pi_1 = Raspberry Pi 3 [part_number=RPI-3-V1.2]
  LED1 = LED - 5mm [color="Blue (470nm)" package="5 mm [THT]"]
  LED2 = LED - 5mm [color="Red (633nm)" package="5 mm [THT]"]
  R1 = Resistor [tolerance=±5% resistance=330 package=THT]
  R2 = Resistor [tolerance=±5% resistance=330 package=THT]
  J2 = JST-VHR-3N [part_number=JST-VHR-3N package=THT]
  LED3 = LED - 5mm [color="Red (633nm)" package="5 mm [THT]"]
  R3 = Resistor [tolerance=±5% resistance=330 package=THT]

nets:
  GND: Raspberry_Pi_1.GND, LED1.cathode, LED2.cathode, J2.pin1, LED3.cathode
  N1: Raspberry_Pi_1.GPIO17, J2.pin2
  3.3V: Raspberry_Pi_1.3V3, R2.Pin_1
  N2: Raspberry_Pi_1.GPIO23, R3.Pin_1
  5V: Raspberry_Pi_1.5V, R1.Pin_1, J2.pin3, J2.pin_6
  N3: LED1.anode, R1.Pin_0
  N4: LED2.anode, R2.Pin_0
  N5: LED3.anode, R3.Pin_0
